# Fritzing sketch pcb-had (saved by Fritzing 0.9.2b)
circuit board: 4.95cm x 4.95cm
breadboards: 1

parts:
  U1 = mystery part, 3 pins [chip_label=?]
  U2 = mystery part, 3 pins [chip_label=?]
  U3 = mystery part, 3 pins [chip_label=?]
  U4 = mystery part, 3 pins [chip_label=?]
  U5 = mystery part, 3 pins [chip_label=?]
  U6 = mystery part, 3 pins [chip_label=?]
  U7 = mystery part, 3 pins [chip_label=?]
  U8 = mystery part, 3 pins [chip_label=?]
  U9 = mystery part, 3 pins [chip_label=?]
  U10 = mystery part, 3 pins [chip_label=?]
  U11 = mystery part, 3 pins [chip_label=?]
  U12 = mystery part, 3 pins [chip_label=?]
  +bat- = mystery part, 2 pins [chip_label=?]
  R1 = Resistor [tolerance=±5% resistance=220 package="0805 [SMD]"]
  R2 = Resistor [tolerance=±5% resistance=220 package="0805 [SMD]"]
  U13 = mystery part, 3 pins [chip_label=?]
  U14 = mystery part, 3 pins [chip_label=?]
  U15 = mystery part, 3 pins [chip_label=?]
  U16 = mystery part, 3 pins [chip_label=?]
  U17 = mystery part, 3 pins [chip_label=?]
  U18 = mystery part, 3 pins [chip_label=?]
  U19 = mystery part, 3 pins [chip_label=?]
  U20 = mystery part, 3 pins [chip_label=?]
  Pad1 = Pad [width=2.54 height=5.08 connect=center]
  on = Pad [width=2.54 height=5.08 connect=center]
  off = Pad [width=2.54 height=5.08 connect=center]  # not connected
  esp-01 = mystery part, 8 pins [chip_label=?]
  R3 = Resistor [tolerance=±5% resistance=220 package="0805 [SMD]"]
  rx_tx_gnd = mystery part, 3 pins [chip_label=?]
  scl_sda_gnd = mystery part, 3 pins [chip_label=?]
  R4 = Resistor [tolerance=±5% resistance=220 package="0805 [SMD]"]
  R5 = Resistor [tolerance=±5% resistance=220 package="0805 [SMD]"]
  J1 = double row female pin header, 6 pins [form="♀ (female)"]
  J2 = female pin header, 12 pins [form="♀ (female)"]
  J3 = female pin header, 12 pins [form="♀ (female)"]
  J4 = female pin header, 2 pins [form="♀ (female)"]
  C1 = Electrolytic Capacitor [capacitance=1µF package="100 mil [THT, electrolytic]"]
  J5 = female pin header, 2 pins [form="♀ (female)"]

nets:
  N1: U1.pin1, U2.pin1, U3.pin1, U4.pin1, U5.pin1, U6.pin1, U13.pin1, U14.pin1, U15.pin1, U16.pin1, U17.pin1, U18.pin1, U19.pin1, U20.pin1, scl_sda_gnd.pin1, J3.pin2, C1.-
  N2: U1.pin2, U2.pin2, U3.pin2, U4.pin2, U5.pin2, U6.pin2, U7.pin2, U8.pin2, U9.pin2, U10.pin2, U11.pin2, U12.pin2, Pad1.pad, esp-01.pin5, R3.Pin_0, R4.Pin_0, J1.pin1, J1.pin2, J3.pin1, C1.+
  N3: U1.pin3, J3.pin12
  N4: U2.pin3, J3.pin11
  N5: U3.pin3, J3.pin10
  N6: U4.pin3, J3.pin8
  N7: U5.pin3, J3.pin7
  N8: U6.pin3, J3.pin6
  N9: U7.pin1, U8.pin1, U9.pin1, U10.pin1, U11.pin1, U12.pin1, +bat-.pin1, esp-01.pin1, rx_tx_gnd.pin1, R5.Pin_0, J1.pin3, J2.pin4
  N10: U7.pin3, J2.pin12
  N11: U8.pin3, J2.pin11
  N12: U9.pin3, J2.pin10
  N13: U10.pin3, J2.pin9
  N14: U11.pin3, J2.pin7
  N15: U12.pin3, J2.pin8
  N16: +bat-.pin2, on.pad
  N17: R1.Pin_0, esp-01.pin2, scl_sda_gnd.pin3, J1.pin5, J4.pin1
  N18: R1.Pin_1, R2.Pin_1, U13.pin2, U14.pin2, U15.pin2, U16.pin2, U17.pin2, U18.pin2, U19.pin2, U20.pin2, J3.pin4
  N19: R2.Pin_0, esp-01.pin3, scl_sda_gnd.pin2, J1.pin4, J4.pin2
  N20: U13.pin3, J2.pin2
  N21: U14.pin3, J2.pin5
  N22: U15.pin3, J2.pin1
  N23: U16.pin3, J5.pin1
  N24: U17.pin3, J3.pin9
  N25: U18.pin3, J5.pin2
  N26: U19.pin3, J3.pin5
  N27: U20.pin3, J2.pin6
  N28: esp-01.pin4, rx_tx_gnd.pin3
  N29: esp-01.pin7, R3.Pin_1
  N30: esp-01.pin8, rx_tx_gnd.pin2
  N31: R4.Pin_1, R5.Pin_1

notes:
  03 02 01 00 A6 A7 13 A3
